// Logisim project Pong.circ as structural Verilog: 1 circuit, main circuit main
module main (
  input  [3:0] in_1,
  input  [3:0] in_2,
  input  in_3,
  input  in_4,
  input  [3:0] in_5,
  input  [3:0] POS___X,
  input  [3:0] POS___Y,
  input  [3:0] in_8,
  input  [3:0] in_9,
  input  [3:0] in_10,
  input  [3:0] in_11,
  input  [3:0] in_12,
  input  [3:0] in_13,
  input  [3:0] in_14,
  input  [3:0] in_15,
  input  [3:0] in_16,
  input  DOWN,
  input  UP,
  input  [3:0] in_19,
  input  [3:0] in_20,
  input  DOWN_2,
  input  UP_2
);

  wire and_1_out, and_5_out, and_6_out, and_7_out, and_9_out, and_10_out, and_11_out, and_12_out, and_13_out,
       and_14_out, and_15_out, and_16_out, and_17_out, and_18_out, and_19_out, and_20_out, and_21_out,
       and_22_out, and_23_out, and_24_out, and_25_out, and_26_out, and_27_out, and_28_out, and_29_out,
       and_30_out, and_31_out, and_32_out, and_33_out, and_34_out, and_35_out, and_36_out, and_37_out,
       and_38_out, and_39_out, and_40_out, and_41_out, and_42_out, and_43_out, and_44_out, and_45_out,
       and_46_out, and_47_out, and_48_out, and_49_out, and_50_out, and_51_out, and_52_out, and_53_out,
       and_54_out, and_55_out, and_56_out, and_57_out, and_58_out, and_59_out, and_60_out, and_61_out,
       and_62_out, and_63_out, and_64_out, and_65_out, and_66_out, and_67_out, and_68_out, and_69_out,
       and_70_out, and_71_out, and_72_out, and_73_out, and_74_out, and_75_out, and_76_out, and_77_out,
       and_78_out, and_79_out, and_80_out, and_81_out, and_82_out, and_83_out, and_84_out, and_85_out,
       and_86_out, and_87_out, and_88_out, and_89_out, and_90_out, and_91_out, and_92_out, and_93_out,
       and_94_out, and_95_out, and_96_out, and_97_out, and_98_out, and_99_out, and_100_out, and_101_out,
       and_102_out, and_103_out, and_104_out, and_105_out, and_106_out, and_107_out, and_108_out,
       and_109_out, and_110_out, and_111_out, and_112_out, and_113_out, and_114_out, and_115_out,
       and_116_out, and_117_out, and_118_out, and_119_out, and_120_out, and_121_out, and_122_out,
       and_123_out, and_124_out, and_125_out, and_126_out, and_127_out, and_128_out, and_129_out,
       and_130_out, and_131_out, and_132_out, and_133_out, and_134_out, and_135_out, and_136_out,
       and_137_out, and_138_out, and_139_out, and_140_out, and_141_out, and_142_out, and_143_out,
       and_144_out, and_145_out, and_146_out, and_147_out, and_148_out, and_149_out, and_150_out,
       and_151_out, and_152_out, and_153_out, and_154_out, and_155_out, and_156_out, and_157_out,
       and_158_out, and_159_out, and_160_out, and_161_out, and_162_out, and_163_out, and_164_out,
       and_165_out, and_166_out, and_167_out, and_168_out, and_169_out, and_170_out, and_171_out,
       and_172_out, and_173_out, and_174_out, and_175_out, and_176_out, and_177_out, and_178_out,
       and_179_out, and_180_out, and_181_out, and_182_out, and_183_out, and_184_out, and_185_out,
       and_186_out, and_187_out, and_188_out, and_189_out, and_190_out, and_191_out, and_192_out,
       and_193_out, and_194_out, and_195_out, and_196_out, and_197_out, and_198_out, and_199_out,
       and_200_out, and_201_out, and_202_out, and_203_out, and_204_out, and_205_out, and_206_out,
       and_207_out, and_208_out, and_209_out, and_210_out, and_211_out, and_212_out, and_213_out,
       and_214_out, and_215_out, and_216_out, and_217_out, and_218_out, and_219_out, and_220_out,
       and_221_out, and_222_out, and_223_out, and_224_out, and_225_out, and_226_out, and_227_out,
       and_228_out, and_229_out, and_230_out, and_231_out, and_232_out, and_233_out, and_234_out,
       and_235_out, and_236_out, and_237_out, and_238_out, and_239_out, and_240_out, and_241_out,
       and_242_out, and_243_out, and_244_out, and_245_out, and_246_out, and_247_out, and_248_out,
       and_249_out, and_250_out, and_251_out, and_252_out, and_253_out, and_254_out, and_255_out,
       and_256_out, and_257_out, and_258_out, and_259_out, and_260_out, and_261_out, and_262_out,
       and_263_out, and_264_out, and_265_out, and_266_out, and_267_out, and_268_out, and_269_out,
       and_270_out, and_271_out, and_272_out, and_273_out, and_274_out, and_275_out, and_276_out,
       and_277_out, and_278_out, and_279_out, and_280_out, and_281_out, and_282_out, and_283_out,
       and_284_out, and_285_out, and_286_out, and_287_out, and_288_out, and_289_out, and_290_out,
       and_291_out, and_292_out, and_293_out, and_294_out, and_295_out, and_296_out, and_297_out,
       and_298_out, and_299_out, and_300_out, and_301_out, and_302_out, and_303_out, and_304_out,
       and_305_out, and_306_out, and_307_out, and_308_out, and_309_out, and_310_out, clock_1_out,
       clock_2_out, clock_3_out, clock_4_out, comparator_1_eq, comparator_2_eq, comparator_3_eq, d_ff_1_q,
       d_ff_1_qn, d_ff_2_q, d_ff_2_qn, demultiplexer_1_out0, demultiplexer_1_out1, demultiplexer_1_out2,
       demultiplexer_1_out3, demultiplexer_2_out0, demultiplexer_2_out1, demultiplexer_2_out2,
       demultiplexer_2_out3, demultiplexer_3_out0, demultiplexer_3_out1, demultiplexer_3_out2,
       demultiplexer_3_out3, demultiplexer_4_out0, demultiplexer_4_out1, demultiplexer_4_out2,
       demultiplexer_4_out3, demultiplexer_5_out0, demultiplexer_5_out1, demultiplexer_5_out2,
       demultiplexer_5_out3, demultiplexer_6_out0, demultiplexer_6_out1, demultiplexer_6_out2,
       demultiplexer_6_out3, demultiplexer_7_out0, demultiplexer_7_out1, demultiplexer_7_out2,
       demultiplexer_7_out3, demultiplexer_8_out0, demultiplexer_8_out1, demultiplexer_8_out2,
       demultiplexer_8_out3, demultiplexer_9_out0, demultiplexer_9_out1, demultiplexer_9_out2,
       demultiplexer_9_out3, demultiplexer_10_out0, demultiplexer_10_out1, demultiplexer_10_out2,
       demultiplexer_10_out3, demultiplexer_11_out0, demultiplexer_11_out1, demultiplexer_11_out2,
       demultiplexer_11_out3, demultiplexer_12_out0, demultiplexer_12_out1, demultiplexer_12_out2,
       demultiplexer_12_out3, demultiplexer_13_out0, demultiplexer_13_out1, demultiplexer_13_out2,
       demultiplexer_13_out3, demultiplexer_14_out0, demultiplexer_14_out1, demultiplexer_14_out2,
       demultiplexer_14_out3, demultiplexer_15_out0, demultiplexer_15_out1, demultiplexer_15_out2,
       demultiplexer_15_out3, demultiplexer_16_out0, demultiplexer_16_out1, demultiplexer_16_out2,
       demultiplexer_16_out3, nor_1_out, nor_2_out, nor_3_out, nor_4_out, nor_5_out, nor_6_out, nor_7_out,
       nor_8_out, not_1_out, not_2_out, not_3_out, not_4_out, not_5_out, not_6_out, not_7_out, not_8_out,
       or_1_out, or_2_out, or_3_out, or_4_out, or_5_out, or_6_out, or_7_out, or_8_out, or_9_out, or_10_out,
       or_11_out, or_12_out, or_13_out, or_14_out, or_15_out, or_16_out, or_17_out, or_18_out, or_19_out,
       or_20_out, or_21_out, or_22_out, or_23_out, or_24_out, or_25_out, or_26_out, or_27_out, or_28_out,
       or_29_out, or_30_out, or_31_out;
  wire [1:0] and_4_out, and_8_out;
  wire [3:0] adder_1_out, adder_2_out, adder_3_out, adder_4_out, adder_5_out, adder_6_out, counter_1_q,
       counter_2_q, counter_3_q, multiplexer_1_out, multiplexer_2_out, multiplexer_3_out, multiplexer_4_out,
       multiplexer_5_out, multiplexer_6_out, multiplexer_7_out, multiplexer_8_out, multiplexer_9_out,
       multiplexer_10_out, multiplexer_11_out, multiplexer_12_out, register_1_q, register_2_q,
       subtractor_1_out, subtractor_2_out, subtractor_3_out, subtractor_4_out, X_POS_q, X_VEL_q, Y_POS_q,
       Y_VEL_q;

  Clock clock_1 (.out(clock_1_out));
  not not_1 (not_1_out, demultiplexer_9_out0);
  Clock clock_2 (.out(clock_2_out));
  not not_2 (not_2_out, demultiplexer_5_out0);
  not not_3 (not_3_out, and_1_out);
  and and_1 (and_1_out, Y_POS_q[3], Y_POS_q[2]);
  and and_2 (and_8_out[1], not_1_out, DOWN_2);
  Multiplexer #(.select(2), .width(4)) multiplexer_1 (
    .in1(adder_2_out), .in2(subtractor_2_out), .out(multiplexer_1_out), .sel(and_4_out));  // open: in0, in3, en
  and and_3 (and_4_out[1], not_2_out, DOWN);
  and and_4 (and_4_out[0], UP, not_4_out);
  and and_5 (and_5_out, 1'b1, nor_1_out);
  nor nor_1 (nor_1_out, and_6_out, and_7_out, and_1_out);
  and and_6 (and_6_out, Y_POS_q[2], nor_2_out);
  nor nor_2 (nor_2_out, and_1_out, and_7_out);
  and and_7 (and_7_out, Y_POS_q[3], not_3_out);
  Register #(.width(4)) register_1 (.D(multiplexer_2_out), .Q(register_1_q), .clk(clock_1_out));  // open: en, clr
  Multiplexer #(.select(2), .width(4)) multiplexer_2 (
    .in1(adder_1_out), .in2(subtractor_1_out), .out(multiplexer_2_out), .sel(and_8_out));  // open: in0, in3, en
  and and_8 (and_8_out[0], UP_2, not_5_out);
  Register #(.width(4)) register_2 (.D(multiplexer_1_out), .Q(register_2_q), .clk(clock_2_out));  // open: en, clr
  not not_4 (not_4_out, demultiplexer_8_out1);
  Demultiplexer #(.select(2)) demultiplexer_1 (
    .out0(demultiplexer_1_out0), .out1(demultiplexer_1_out1), .out2(demultiplexer_1_out2),
    .out3(demultiplexer_1_out3), .in(and_5_out), .sel(Y_POS_q[1:0]));  // open: en
  Demultiplexer #(.select(2)) demultiplexer_2 (
    .out0(demultiplexer_2_out0), .out1(demultiplexer_2_out1), .out2(demultiplexer_2_out2),
    .out3(demultiplexer_2_out3), .in(and_6_out), .sel(Y_POS_q[1:0]));  // open: en
  Demultiplexer #(.select(2)) demultiplexer_3 (
    .out0(demultiplexer_3_out0), .out1(demultiplexer_3_out1), .out2(demultiplexer_3_out2),
    .out3(demultiplexer_3_out3), .in(and_7_out), .sel(Y_POS_q[1:0]));  // open: en
  Demultiplexer #(.select(2)) demultiplexer_4 (
    .out0(demultiplexer_4_out0), .out1(demultiplexer_4_out1), .out2(demultiplexer_4_out2),
    .out3(demultiplexer_4_out3), .in(and_1_out), .sel(Y_POS_q[1:0]));  // open: en
  Adder #(.width(4)) adder_1 (.a(register_1_q), .b(in_19), .out(adder_1_out));  // open: cin, cout
  Subtractor #(.width(4)) subtractor_1 (.a(register_1_q), .b(in_20), .out(subtractor_1_out));  // open: bin, bout
  not not_5 (not_5_out, demultiplexer_12_out1);
  Adder #(.width(4)) adder_2 (.a(register_2_q), .b(in_15), .out(adder_2_out));  // open: cin, cout
  Subtractor #(.width(4)) subtractor_2 (.a(register_2_q), .b(in_16), .out(subtractor_2_out));  // open: bin, bout
  Adder #(.width(4)) adder_3 (.a(register_2_q), .b(in_12), .out(adder_3_out));  // open: cin, cout
  Adder #(.width(4)) adder_4 (.a(register_2_q), .b(in_14), .out(adder_4_out));  // open: cin, cout
  and and_9 (and_9_out, register_2_q[3], register_2_q[2]);
  not not_6 (not_6_out, and_10_out);
  and and_10 (and_10_out, register_1_q[3], register_1_q[2]);
  Comparator #(.width(4), .mode("unsigned")) comparator_1 (
    .a(register_2_q), .b(Y_POS_q), .eq(comparator_1_eq));  // open: gt, lt
  Comparator #(.width(4), .mode("unsigned")) comparator_2 (
    .a(adder_3_out), .b(Y_POS_q), .eq(comparator_2_eq));  // open: gt, lt
  Comparator #(.width(4), .mode("unsigned")) comparator_3 (
    .a(adder_4_out), .b(Y_POS_q), .eq(comparator_3_eq));  // open: gt, lt
  nor nor_3 (nor_3_out, and_16_out, and_11_out, and_9_out);
  and and_11 (and_11_out, register_2_q[3], not_7_out);
  not not_7 (not_7_out, and_9_out);
  and and_12 (and_12_out, 1'b1, nor_4_out);
  nor nor_4 (nor_4_out, and_13_out, and_14_out, and_10_out);
  and and_13 (and_13_out, register_1_q[2], nor_5_out);
  nor nor_5 (nor_5_out, and_10_out, and_14_out);
  and and_14 (and_14_out, register_1_q[3], not_6_out);
  or or_1 (or_1_out, comparator_1_eq, comparator_2_eq, comparator_3_eq);
  and and_15 (and_15_out, 1'b1, nor_3_out);
  Demultiplexer #(.select(2)) demultiplexer_5 (
    .out0(demultiplexer_5_out0), .out1(demultiplexer_5_out1), .out2(demultiplexer_5_out2),
    .out3(demultiplexer_5_out3), .in(and_15_out), .sel(register_2_q[1:0]));  // open: en
  Demultiplexer #(.select(2)) demultiplexer_6 (
    .out0(demultiplexer_6_out0), .out1(demultiplexer_6_out1), .out2(demultiplexer_6_out2),
    .out3(demultiplexer_6_out3), .in(and_16_out), .sel(register_2_q[1:0]));  // open: en
  and and_16 (and_16_out, register_2_q[2], nor_6_out);
  nor nor_6 (nor_6_out, and_9_out, and_11_out);
  Demultiplexer #(.select(2)) demultiplexer_7 (
    .out0(demultiplexer_7_out0), .out1(demultiplexer_7_out1), .out2(demultiplexer_7_out2),
    .out3(demultiplexer_7_out3), .in(and_11_out), .sel(register_2_q[1:0]));  // open: en
  Demultiplexer #(.select(2)) demultiplexer_8 (
    .out0(demultiplexer_8_out0), .out1(demultiplexer_8_out1), .out2(demultiplexer_8_out2),
    .out3(demultiplexer_8_out3), .in(and_9_out), .sel(register_2_q[1:0]));  // open: en
  Demultiplexer #(.select(2)) demultiplexer_9 (
    .out0(demultiplexer_9_out0), .out1(demultiplexer_9_out1), .out2(demultiplexer_9_out2),
    .out3(demultiplexer_9_out3), .in(and_12_out), .sel(register_1_q[1:0]));  // open: en
  Demultiplexer #(.select(2)) demultiplexer_10 (
    .out0(demultiplexer_10_out0), .out1(demultiplexer_10_out1), .out2(demultiplexer_10_out2),
    .out3(demultiplexer_10_out3), .in(and_13_out), .sel(register_1_q[1:0]));  // open: en
  Demultiplexer #(.select(2)) demultiplexer_11 (
    .out0(demultiplexer_11_out0), .out1(demultiplexer_11_out1), .out2(demultiplexer_11_out2),
    .out3(demultiplexer_11_out3), .in(and_14_out), .sel(register_1_q[1:0]));  // open: en
  Demultiplexer #(.select(2)) demultiplexer_12 (
    .out0(demultiplexer_12_out0), .out1(demultiplexer_12_out1), .out2(demultiplexer_12_out2),
    .out3(demultiplexer_12_out3), .in(and_10_out), .sel(register_1_q[1:0]));  // open: en
  or or_2 (or_2_out, demultiplexer_5_out0, demultiplexer_5_out1);
  or or_3 (or_3_out, demultiplexer_5_out0, demultiplexer_5_out1, demultiplexer_5_out2);
  or or_4 (or_4_out, demultiplexer_5_out1, demultiplexer_5_out2, demultiplexer_5_out3);
  or or_5 (or_5_out, demultiplexer_5_out2, demultiplexer_5_out3, demultiplexer_6_out0);
  or or_6 (or_6_out, demultiplexer_5_out3, demultiplexer_6_out0, demultiplexer_6_out1);
  or or_7 (or_7_out, demultiplexer_6_out0, demultiplexer_6_out1, demultiplexer_6_out2);
  or or_8 (or_8_out, demultiplexer_6_out1, demultiplexer_6_out2, demultiplexer_6_out3);
  or or_9 (or_9_out, demultiplexer_6_out2, demultiplexer_6_out3, demultiplexer_7_out0);
  or or_10 (or_10_out, demultiplexer_6_out3, demultiplexer_7_out0, demultiplexer_7_out1);
  or or_11 (or_11_out, demultiplexer_7_out0, demultiplexer_7_out1, demultiplexer_7_out2);
  or or_12 (or_12_out, demultiplexer_7_out1, demultiplexer_7_out2, demultiplexer_7_out3);
  or or_13 (or_13_out, demultiplexer_7_out2, demultiplexer_7_out3, demultiplexer_8_out0);
  or or_14 (or_14_out, demultiplexer_7_out3, demultiplexer_8_out0, demultiplexer_8_out1, demultiplexer_8_out2, demultiplexer_8_out3);
  or or_15 (or_15_out, demultiplexer_8_out0, demultiplexer_8_out1, demultiplexer_8_out2, demultiplexer_8_out3);
  or or_16 (or_16_out, demultiplexer_8_out1, demultiplexer_8_out2, demultiplexer_8_out3);
  Clock clock_3 (.out(clock_3_out));
  and and_17 (and_17_out, 1'b1, demultiplexer_5_out0);
  LED led_1 (.in(and_17_out));
  and and_18 (and_18_out, 1'b1, or_2_out);
  LED led_2 (.in(and_18_out));
  LED led_3 (.in(and_19_out));
  and and_19 (and_19_out, 1'b1, or_3_out);
  LED led_4 (.in(and_20_out));
  and and_20 (and_20_out, 1'b1, or_4_out);
  LED led_5 (.in(and_21_out));
  and and_21 (and_21_out, 1'b1, or_5_out);
  and and_22 (and_22_out, 1'b1, or_6_out);
  LED led_6 (.in(and_22_out));
  and and_23 (and_23_out, 1'b1, or_7_out);
  LED led_7 (.in(and_23_out));
  LED led_8 (.in(and_24_out));
  and and_24 (and_24_out, 1'b1, or_8_out);
  LED led_9 (.in(and_25_out));
  and and_25 (and_25_out, 1'b1, or_9_out);
  LED led_10 (.in(and_26_out));
  and and_26 (and_26_out, 1'b1, or_10_out);
  LED led_11 (.in(and_27_out));
  and and_27 (and_27_out, 1'b1, or_11_out);
  and and_28 (and_28_out, 1'b1, or_12_out);
  LED led_12 (.in(and_28_out));
  and and_29 (and_29_out, 1'b1, or_13_out);
  LED led_13 (.in(and_29_out));
  LED led_14 (.in(and_30_out));
  and and_30 (and_30_out, 1'b1, or_14_out);
  and and_31 (and_31_out, 1'b1, or_15_out);
  LED led_15 (.in(and_31_out));
  LED led_16 (.in(and_32_out));
  and and_32 (and_32_out, 1'b1, or_16_out);
  Counter #(.width(4), .max('hf)) counter_1 (
    .count(1'b1), .Q(counter_1_q), .clk(clock_3_out), .clr(in_3));  // open: load, D, carry
  or or_17 (or_17_out, demultiplexer_9_out0, demultiplexer_9_out1);
  or or_18 (or_18_out, demultiplexer_9_out0, demultiplexer_9_out1, demultiplexer_9_out2);
  or or_19 (or_19_out, demultiplexer_9_out1, demultiplexer_9_out2, demultiplexer_9_out3);
  or or_20 (or_20_out, demultiplexer_9_out2, demultiplexer_9_out3, demultiplexer_10_out0);
  or or_21 (or_21_out, demultiplexer_9_out3, demultiplexer_10_out0, demultiplexer_10_out1);
  or or_22 (or_22_out, demultiplexer_10_out0, demultiplexer_10_out1, demultiplexer_10_out2);
  or or_23 (or_23_out, demultiplexer_10_out1, demultiplexer_10_out2, demultiplexer_10_out3);
  or or_24 (or_24_out, demultiplexer_10_out2, demultiplexer_10_out3, demultiplexer_11_out0);
  or or_25 (or_25_out, demultiplexer_10_out3, demultiplexer_11_out0, demultiplexer_11_out1);
  or or_26 (or_26_out, demultiplexer_11_out0, demultiplexer_11_out1, demultiplexer_11_out2);
  or or_27 (or_27_out, demultiplexer_11_out1, demultiplexer_11_out2, demultiplexer_11_out3);
  or or_28 (or_28_out, demultiplexer_11_out2, demultiplexer_11_out3, demultiplexer_12_out0);
  or or_29 (or_29_out, demultiplexer_11_out3, demultiplexer_12_out0, demultiplexer_12_out1, demultiplexer_12_out2, demultiplexer_12_out3);
  or or_30 (or_30_out, demultiplexer_12_out0, demultiplexer_12_out1, demultiplexer_12_out2, demultiplexer_12_out3);
  or or_31 (or_31_out, demultiplexer_12_out1, demultiplexer_12_out2, demultiplexer_12_out3);
  LED led_17 (.in(and_33_out));
  and and_33 (and_33_out, 1'b1, demultiplexer_9_out0);
  LED led_18 (.in(and_34_out));
  and and_34 (and_34_out, 1'b1, or_17_out);
  LED led_19 (.in(and_35_out));
  and and_35 (and_35_out, 1'b1, or_18_out);
  and and_36 (and_36_out, 1'b1, or_19_out);
  LED led_20 (.in(and_36_out));
  and and_37 (and_37_out, 1'b1, or_20_out);
  LED led_21 (.in(and_37_out));
  and and_38 (and_38_out, 1'b1, or_21_out);
  LED led_22 (.in(and_38_out));
  and and_39 (and_39_out, 1'b1, or_22_out);
  LED led_23 (.in(and_39_out));
  and and_40 (and_40_out, 1'b1, or_23_out);
  LED led_24 (.in(and_40_out));
  and and_41 (and_41_out, 1'b1, or_24_out);
  LED led_25 (.in(and_41_out));
  and and_42 (and_42_out, 1'b1, or_25_out);
  LED led_26 (.in(and_42_out));
  and and_43 (and_43_out, 1'b1, or_26_out);
  LED led_27 (.in(and_43_out));
  LED led_28 (.in(and_44_out));
  and and_44 (and_44_out, 1'b1, or_27_out);
  LED led_29 (.in(and_45_out));
  and and_45 (and_45_out, 1'b1, or_28_out);
  LED led_30 (.in(and_46_out));
  and and_46 (and_46_out, 1'b1, or_29_out);
  and and_47 (and_47_out, 1'b1, or_30_out);
  LED led_31 (.in(and_47_out));
  and and_48 (and_48_out, 1'b1, or_31_out);
  LED led_32 (.in(and_48_out));
  and and_49 (and_49_out, counter_1_q[0], counter_1_q[1], counter_1_q[2], counter_1_q[3]);
  LED led_33 (.in(counter_2_q[0]));
  LED led_34 (.in(counter_2_q[1]));
  LED led_35 (.in(counter_2_q[2]));
  LED led_36 (.in(counter_2_q[3]));
  Counter #(.width(4), .max('hf)) counter_2 (.Q(counter_2_q), .clk(and_66_out));  // open: load, D, count, carry, clr
  Counter #(.width(4), .max('hf)) counter_3 (
    .count(1'b1), .Q(counter_3_q), .clk(and_49_out), .clr(in_4));  // open: load, D, carry
  and and_50 (and_50_out, 1'b1, demultiplexer_5_out0);
  LED led_37 (.in(and_50_out));
  and and_51 (and_51_out, 1'b1, or_2_out);
  LED led_38 (.in(and_51_out));
  and and_52 (and_52_out, 1'b1, or_3_out);
  LED led_39 (.in(and_52_out));
  and and_53 (and_53_out, 1'b1, or_4_out);
  LED led_40 (.in(and_53_out));
  LED led_41 (.in(and_54_out));
  and and_54 (and_54_out, 1'b1, or_5_out);
  and and_55 (and_55_out, 1'b1, or_6_out);
  LED led_42 (.in(and_55_out));
  LED led_43 (.in(and_56_out));
  and and_56 (and_56_out, 1'b1, or_7_out);
  and and_57 (and_57_out, 1'b1, or_8_out);
  LED led_44 (.in(and_57_out));
  and and_58 (and_58_out, 1'b1, or_9_out);
  LED led_45 (.in(and_58_out));
  and and_59 (and_59_out, 1'b1, or_10_out);
  LED led_46 (.in(and_59_out));
  and and_60 (and_60_out, 1'b1, or_11_out);
  LED led_47 (.in(and_60_out));
  and and_61 (and_61_out, 1'b1, or_12_out);
  LED led_48 (.in(and_61_out));
  LED led_49 (.in(and_62_out));
  and and_62 (and_62_out, 1'b1, or_13_out);
  LED led_50 (.in(and_63_out));
  and and_63 (and_63_out, 1'b1, or_14_out);
  LED led_51 (.in(and_64_out));
  and and_64 (and_64_out, 1'b1, or_15_out);
  LED led_52 (.in(and_65_out));
  and and_65 (and_65_out, 1'b1, or_16_out);
  and and_66 (and_66_out, demultiplexer_13_out1, or_1_out);
  LED led_53 (.in(and_68_out));
  and and_67 (and_67_out, demultiplexer_13_out2, demultiplexer_1_out0);
  LED led_54 (.in(and_67_out));
  and and_68 (and_68_out, demultiplexer_13_out1, demultiplexer_1_out0);
  LED led_55 (.in(and_70_out));
  LED led_56 (.in(and_69_out));
  and and_69 (and_69_out, demultiplexer_13_out2, demultiplexer_1_out1);
  and and_70 (and_70_out, demultiplexer_13_out1, demultiplexer_1_out1);
  and and_71 (and_71_out, demultiplexer_13_out1, demultiplexer_1_out2);
  LED led_57 (.in(and_71_out));
  and and_72 (and_72_out, demultiplexer_13_out2, demultiplexer_1_out2);
  LED led_58 (.in(and_72_out));
  LED led_59 (.in(and_74_out));
  and and_73 (and_73_out, demultiplexer_13_out2, demultiplexer_1_out3);
  and and_74 (and_74_out, demultiplexer_13_out1, demultiplexer_1_out3);
  LED led_60 (.in(and_73_out));
  and and_75 (and_75_out, demultiplexer_13_out1, demultiplexer_2_out0);
  LED led_61 (.in(and_75_out));
  LED led_62 (.in(and_76_out));
  and and_76 (and_76_out, demultiplexer_13_out2, demultiplexer_2_out0);
  LED led_63 (.in(and_78_out));
  and and_77 (and_77_out, demultiplexer_13_out1, demultiplexer_2_out1);
  and and_78 (and_78_out, demultiplexer_13_out2, demultiplexer_2_out1);
  LED led_64 (.in(and_77_out));
  and and_79 (and_79_out, demultiplexer_13_out2, demultiplexer_2_out2);
  and and_80 (and_80_out, demultiplexer_13_out1, demultiplexer_2_out2);
  LED led_65 (.in(and_79_out));
  LED led_66 (.in(and_80_out));
  and and_81 (and_81_out, demultiplexer_13_out2, demultiplexer_2_out3);
  and and_82 (and_82_out, demultiplexer_13_out1, demultiplexer_2_out3);
  LED led_67 (.in(and_81_out));
  LED led_68 (.in(and_82_out));
  and and_83 (and_83_out, demultiplexer_13_out2, demultiplexer_3_out0);
  LED led_69 (.in(and_83_out));
  LED led_70 (.in(and_84_out));
  and and_84 (and_84_out, demultiplexer_13_out1, demultiplexer_3_out0);
  and and_85 (and_85_out, demultiplexer_13_out1, demultiplexer_3_out1);
  LED led_71 (.in(and_85_out));
  and and_86 (and_86_out, demultiplexer_13_out2, demultiplexer_3_out1);
  LED led_72 (.in(and_86_out));
  LED led_73 (.in(and_87_out));
  LED led_74 (.in(and_88_out));
  and and_87 (and_87_out, demultiplexer_13_out2, demultiplexer_3_out2);
  and and_88 (and_88_out, demultiplexer_13_out1, demultiplexer_3_out2);
  and and_89 (and_89_out, demultiplexer_13_out2, demultiplexer_3_out3);
  LED led_75 (.in(and_90_out));
  and and_90 (and_90_out, demultiplexer_13_out1, demultiplexer_3_out3);
  LED led_76 (.in(and_89_out));
  and and_91 (and_91_out, demultiplexer_13_out1, demultiplexer_4_out0);
  and and_92 (and_92_out, demultiplexer_13_out2, demultiplexer_4_out0);
  LED led_77 (.in(and_91_out));
  LED led_78 (.in(and_92_out));
  and and_93 (and_93_out, demultiplexer_13_out1, demultiplexer_4_out1);
  LED led_79 (.in(and_94_out));
  LED led_80 (.in(and_93_out));
  and and_94 (and_94_out, demultiplexer_13_out2, demultiplexer_4_out1);
  LED led_81 (.in(and_95_out));
  LED led_82 (.in(and_96_out));
  and and_95 (and_95_out, demultiplexer_13_out1, demultiplexer_4_out2);
  and and_96 (and_96_out, demultiplexer_13_out2, demultiplexer_4_out2);
  and and_97 (and_97_out, demultiplexer_13_out1, demultiplexer_4_out3);
  LED led_83 (.in(and_97_out));
  and and_98 (and_98_out, demultiplexer_13_out2, demultiplexer_4_out3);
  LED led_84 (.in(and_98_out));
  and and_99 (and_99_out, demultiplexer_13_out3, demultiplexer_1_out0);
  LED led_85 (.in(and_99_out));
  LED led_86 (.in(and_100_out));
  and and_100 (and_100_out, demultiplexer_13_out3, demultiplexer_1_out1);
  and and_101 (and_101_out, demultiplexer_13_out3, demultiplexer_1_out2);
  LED led_87 (.in(and_101_out));
  LED led_88 (.in(and_102_out));
  and and_102 (and_102_out, demultiplexer_13_out3, demultiplexer_1_out3);
  LED led_89 (.in(and_103_out));
  and and_103 (and_103_out, demultiplexer_13_out3, demultiplexer_2_out0);
  LED led_90 (.in(and_104_out));
  and and_104 (and_104_out, demultiplexer_13_out3, demultiplexer_2_out1);
  LED led_91 (.in(and_105_out));
  and and_105 (and_105_out, demultiplexer_13_out3, demultiplexer_2_out2);
  and and_106 (and_106_out, demultiplexer_13_out3, demultiplexer_2_out3);
  LED led_92 (.in(and_106_out));
  and and_107 (and_107_out, demultiplexer_13_out3, demultiplexer_3_out0);
  LED led_93 (.in(and_107_out));
  LED led_94 (.in(and_108_out));
  and and_108 (and_108_out, demultiplexer_13_out3, demultiplexer_3_out1);
  and and_109 (and_109_out, demultiplexer_13_out3, demultiplexer_3_out2);
  LED led_95 (.in(and_109_out));
  LED led_96 (.in(and_110_out));
  and and_110 (and_110_out, demultiplexer_13_out3, demultiplexer_3_out3);
  and and_111 (and_111_out, demultiplexer_13_out3, demultiplexer_4_out0);
  LED led_97 (.in(and_111_out));
  and and_112 (and_112_out, demultiplexer_13_out3, demultiplexer_4_out1);
  LED led_98 (.in(and_112_out));
  LED led_99 (.in(and_113_out));
  and and_113 (and_113_out, demultiplexer_13_out3, demultiplexer_4_out2);
  and and_114 (and_114_out, demultiplexer_13_out3, demultiplexer_4_out3);
  LED led_100 (.in(and_114_out));
  and and_115 (and_115_out, demultiplexer_14_out0, demultiplexer_1_out0);
  LED led_101 (.in(and_115_out));
  LED led_102 (.in(and_116_out));
  and and_116 (and_116_out, demultiplexer_14_out0, demultiplexer_1_out1);
  LED led_103 (.in(and_117_out));
  and and_117 (and_117_out, demultiplexer_14_out0, demultiplexer_1_out2);
  LED led_104 (.in(and_118_out));
  and and_118 (and_118_out, demultiplexer_14_out0, demultiplexer_1_out3);
  LED led_105 (.in(and_119_out));
  and and_119 (and_119_out, demultiplexer_14_out0, demultiplexer_2_out0);
  LED led_106 (.in(and_120_out));
  and and_120 (and_120_out, demultiplexer_14_out0, demultiplexer_2_out1);
  LED led_107 (.in(and_121_out));
  and and_121 (and_121_out, demultiplexer_14_out0, demultiplexer_2_out2);
  LED led_108 (.in(and_122_out));
  and and_122 (and_122_out, demultiplexer_14_out0, demultiplexer_2_out3);
  and and_123 (and_123_out, demultiplexer_14_out0, demultiplexer_3_out0);
  LED led_109 (.in(and_123_out));
  LED led_110 (.in(and_124_out));
  and and_124 (and_124_out, demultiplexer_14_out0, demultiplexer_3_out1);
  and and_125 (and_125_out, demultiplexer_14_out0, demultiplexer_3_out2);
  LED led_111 (.in(and_125_out));
  and and_126 (and_126_out, demultiplexer_14_out0, demultiplexer_3_out3);
  LED led_112 (.in(and_126_out));
  LED led_113 (.in(and_127_out));
  and and_127 (and_127_out, demultiplexer_14_out0, demultiplexer_4_out0);
  and and_128 (and_128_out, demultiplexer_14_out0, demultiplexer_4_out1);
  LED led_114 (.in(and_128_out));
  LED led_115 (.in(and_129_out));
  and and_129 (and_129_out, demultiplexer_14_out0, demultiplexer_4_out2);
  and and_130 (and_130_out, demultiplexer_14_out0, demultiplexer_4_out3);
  LED led_116 (.in(and_130_out));
  nor nor_7 (nor_7_out, and_198_out, and_181_out, and_148_out);
  and and_131 (and_131_out, nor_7_out, 1'b1);
  Demultiplexer #(.select(2)) demultiplexer_13 (
    .out0(demultiplexer_13_out0), .out1(demultiplexer_13_out1), .out2(demultiplexer_13_out2),
    .out3(demultiplexer_13_out3), .in(and_131_out), .sel(X_POS_q[1:0]));  // open: en
  and and_132 (and_132_out, demultiplexer_14_out1, demultiplexer_1_out0);
  LED led_117 (.in(and_132_out));
  and and_133 (and_133_out, demultiplexer_14_out1, demultiplexer_1_out1);
  LED led_118 (.in(and_133_out));
  LED led_119 (.in(and_134_out));
  and and_134 (and_134_out, demultiplexer_14_out1, demultiplexer_1_out2);
  LED led_120 (.in(and_135_out));
  and and_135 (and_135_out, demultiplexer_14_out1, demultiplexer_1_out3);
  LED led_121 (.in(and_136_out));
  and and_136 (and_136_out, demultiplexer_14_out1, demultiplexer_2_out0);
  and and_137 (and_137_out, demultiplexer_14_out1, demultiplexer_2_out1);
  LED led_122 (.in(and_137_out));
  and and_138 (and_138_out, demultiplexer_14_out1, demultiplexer_2_out2);
  LED led_123 (.in(and_138_out));
  LED led_124 (.in(and_139_out));
  and and_139 (and_139_out, demultiplexer_14_out1, demultiplexer_2_out3);
  LED led_125 (.in(and_140_out));
  and and_140 (and_140_out, demultiplexer_14_out1, demultiplexer_3_out0);
  and and_141 (and_141_out, demultiplexer_14_out1, demultiplexer_3_out1);
  LED led_126 (.in(and_141_out));
  and and_142 (and_142_out, demultiplexer_14_out1, demultiplexer_3_out2);
  LED led_127 (.in(and_142_out));
  and and_143 (and_143_out, demultiplexer_14_out1, demultiplexer_3_out3);
  LED led_128 (.in(and_143_out));
  LED led_129 (.in(and_144_out));
  and and_144 (and_144_out, demultiplexer_14_out1, demultiplexer_4_out0);
  and and_145 (and_145_out, demultiplexer_14_out1, demultiplexer_4_out1);
  LED led_130 (.in(and_145_out));
  and and_146 (and_146_out, demultiplexer_14_out1, demultiplexer_4_out2);
  LED led_131 (.in(and_146_out));
  and and_147 (and_147_out, demultiplexer_14_out1, demultiplexer_4_out3);
  LED led_132 (.in(and_147_out));
  and and_148 (and_148_out, nor_8_out, X_POS_q[2]);
  Demultiplexer #(.select(2)) demultiplexer_14 (
    .out0(demultiplexer_14_out0), .out1(demultiplexer_14_out1), .out2(demultiplexer_14_out2),
    .out3(demultiplexer_14_out3), .in(and_148_out), .sel(X_POS_q[1:0]));  // open: en
  LED led_133 (.in(and_149_out));
  and and_149 (and_149_out, demultiplexer_14_out2, demultiplexer_1_out0);
  and and_150 (and_150_out, demultiplexer_14_out2, demultiplexer_1_out1);
  LED led_134 (.in(and_150_out));
  LED led_135 (.in(and_151_out));
  and and_151 (and_151_out, demultiplexer_14_out2, demultiplexer_1_out2);
  and and_152 (and_152_out, demultiplexer_14_out2, demultiplexer_1_out3);
  LED led_136 (.in(and_152_out));
  LED led_137 (.in(and_153_out));
  and and_153 (and_153_out, demultiplexer_14_out2, demultiplexer_2_out0);
  LED led_138 (.in(and_154_out));
  and and_154 (and_154_out, demultiplexer_14_out2, demultiplexer_2_out1);
  LED led_139 (.in(and_155_out));
  and and_155 (and_155_out, demultiplexer_14_out2, demultiplexer_2_out2);
  LED led_140 (.in(and_156_out));
  and and_156 (and_156_out, demultiplexer_14_out2, demultiplexer_2_out3);
  and and_157 (and_157_out, demultiplexer_14_out2, demultiplexer_3_out0);
  LED led_141 (.in(and_157_out));
  and and_158 (and_158_out, demultiplexer_14_out2, demultiplexer_3_out1);
  LED led_142 (.in(and_158_out));
  and and_159 (and_159_out, demultiplexer_14_out2, demultiplexer_3_out2);
  LED led_143 (.in(and_159_out));
  and and_160 (and_160_out, demultiplexer_14_out2, demultiplexer_3_out3);
  LED led_144 (.in(and_160_out));
  LED led_145 (.in(and_161_out));
  and and_161 (and_161_out, demultiplexer_14_out2, demultiplexer_4_out0);
  LED led_146 (.in(and_162_out));
  and and_162 (and_162_out, demultiplexer_14_out2, demultiplexer_4_out1);
  LED led_147 (.in(and_163_out));
  and and_163 (and_163_out, demultiplexer_14_out2, demultiplexer_4_out2);
  and and_164 (and_164_out, demultiplexer_14_out2, demultiplexer_4_out3);
  LED led_148 (.in(and_164_out));
  nor nor_8 (nor_8_out, and_198_out, and_181_out);
  LED led_149 (.in(and_165_out));
  and and_165 (and_165_out, demultiplexer_14_out3, demultiplexer_1_out0);
  LED led_150 (.in(and_166_out));
  and and_166 (and_166_out, demultiplexer_14_out3, demultiplexer_1_out1);
  and and_167 (and_167_out, demultiplexer_14_out3, demultiplexer_1_out2);
  LED led_151 (.in(and_167_out));
  LED led_152 (.in(and_168_out));
  and and_168 (and_168_out, demultiplexer_14_out3, demultiplexer_1_out3);
  LED led_153 (.in(and_169_out));
  and and_169 (and_169_out, demultiplexer_14_out3, demultiplexer_2_out0);
  LED led_154 (.in(and_170_out));
  and and_170 (and_170_out, demultiplexer_14_out3, demultiplexer_2_out1);
  LED led_155 (.in(and_171_out));
  and and_171 (and_171_out, demultiplexer_14_out3, demultiplexer_2_out2);
  and and_172 (and_172_out, demultiplexer_14_out3, demultiplexer_2_out3);
  LED led_156 (.in(and_172_out));
  and and_173 (and_173_out, demultiplexer_14_out3, demultiplexer_3_out0);
  LED led_157 (.in(and_173_out));
  and and_174 (and_174_out, demultiplexer_14_out3, demultiplexer_3_out1);
  LED led_158 (.in(and_174_out));
  LED led_159 (.in(and_175_out));
  and and_175 (and_175_out, demultiplexer_14_out3, demultiplexer_3_out2);
  and and_176 (and_176_out, demultiplexer_14_out3, demultiplexer_3_out3);
  LED led_160 (.in(and_176_out));
  and and_177 (and_177_out, demultiplexer_14_out3, demultiplexer_4_out0);
  LED led_161 (.in(and_177_out));
  and and_178 (and_178_out, demultiplexer_14_out3, demultiplexer_4_out1);
  LED led_162 (.in(and_178_out));
  LED led_163 (.in(and_179_out));
  and and_179 (and_179_out, demultiplexer_14_out3, demultiplexer_4_out2);
  and and_180 (and_180_out, demultiplexer_14_out3, demultiplexer_4_out3);
  LED led_164 (.in(and_180_out));
  and and_181 (and_181_out, not_8_out, X_POS_q[3]);
  Demultiplexer #(.select(2)) demultiplexer_15 (
    .out0(demultiplexer_15_out0), .out1(demultiplexer_15_out1), .out2(demultiplexer_15_out2),
    .out3(demultiplexer_15_out3), .in(and_181_out), .sel(X_POS_q[1:0]));  // open: en
  LED led_165 (.in(and_182_out));
  and and_182 (and_182_out, demultiplexer_15_out0, demultiplexer_1_out0);
  and and_183 (and_183_out, demultiplexer_15_out0, demultiplexer_1_out1);
  LED led_166 (.in(and_183_out));
  LED led_167 (.in(and_184_out));
  and and_184 (and_184_out, demultiplexer_15_out0, demultiplexer_1_out2);
  LED led_168 (.in(and_185_out));
  and and_185 (and_185_out, demultiplexer_15_out0, demultiplexer_1_out3);
  LED led_169 (.in(and_186_out));
  and and_186 (and_186_out, demultiplexer_15_out0, demultiplexer_2_out0);
  and and_187 (and_187_out, demultiplexer_15_out0, demultiplexer_2_out1);
  LED led_170 (.in(and_187_out));
  and and_188 (and_188_out, demultiplexer_15_out0, demultiplexer_2_out2);
  LED led_171 (.in(and_188_out));
  and and_189 (and_189_out, demultiplexer_15_out0, demultiplexer_2_out3);
  LED led_172 (.in(and_189_out));
  and and_190 (and_190_out, demultiplexer_15_out0, demultiplexer_3_out0);
  LED led_173 (.in(and_190_out));
  LED led_174 (.in(and_191_out));
  and and_191 (and_191_out, demultiplexer_15_out0, demultiplexer_3_out1);
  LED led_175 (.in(and_192_out));
  and and_192 (and_192_out, demultiplexer_15_out0, demultiplexer_3_out2);
  LED led_176 (.in(and_193_out));
  and and_193 (and_193_out, demultiplexer_15_out0, demultiplexer_3_out3);
  and and_194 (and_194_out, demultiplexer_15_out0, demultiplexer_4_out0);
  LED led_177 (.in(and_194_out));
  and and_195 (and_195_out, demultiplexer_15_out0, demultiplexer_4_out1);
  LED led_178 (.in(and_195_out));
  and and_196 (and_196_out, demultiplexer_15_out0, demultiplexer_4_out2);
  LED led_179 (.in(and_196_out));
  and and_197 (and_197_out, demultiplexer_15_out0, demultiplexer_4_out3);
  LED led_180 (.in(and_197_out));
  not not_8 (not_8_out, and_198_out);
  and and_198 (and_198_out, X_POS_q[2], X_POS_q[3]);
  and and_199 (and_199_out, demultiplexer_15_out2, demultiplexer_1_out0);
  and and_200 (and_200_out, demultiplexer_15_out1, demultiplexer_1_out0);
  LED led_181 (.in(and_199_out));
  LED led_182 (.in(and_200_out));
  and and_201 (and_201_out, demultiplexer_15_out1, demultiplexer_1_out1);
  and and_202 (and_202_out, demultiplexer_15_out2, demultiplexer_1_out1);
  LED led_183 (.in(and_201_out));
  LED led_184 (.in(and_202_out));
  LED led_185 (.in(and_204_out));
  LED led_186 (.in(and_203_out));
  and and_203 (and_203_out, demultiplexer_15_out1, demultiplexer_1_out2);
  and and_204 (and_204_out, demultiplexer_15_out2, demultiplexer_1_out2);
  and and_205 (and_205_out, demultiplexer_15_out2, demultiplexer_1_out3);
  LED led_187 (.in(and_205_out));
  and and_206 (and_206_out, demultiplexer_15_out1, demultiplexer_1_out3);
  LED led_188 (.in(and_206_out));
  LED led_189 (.in(and_208_out));
  LED led_190 (.in(and_207_out));
  and and_207 (and_207_out, demultiplexer_15_out2, demultiplexer_2_out0);
  and and_208 (and_208_out, demultiplexer_15_out1, demultiplexer_2_out0);
  and and_209 (and_209_out, demultiplexer_15_out1, demultiplexer_2_out1);
  and and_210 (and_210_out, demultiplexer_15_out2, demultiplexer_2_out1);
  LED led_191 (.in(and_210_out));
  LED led_192 (.in(and_209_out));
  LED led_193 (.in(and_211_out));
  LED led_194 (.in(and_212_out));
  and and_211 (and_211_out, demultiplexer_15_out2, demultiplexer_2_out2);
  and and_212 (and_212_out, demultiplexer_15_out1, demultiplexer_2_out2);
  LED led_195 (.in(and_214_out));
  and and_213 (and_213_out, demultiplexer_15_out2, demultiplexer_2_out3);
  LED led_196 (.in(and_213_out));
  and and_214 (and_214_out, demultiplexer_15_out1, demultiplexer_2_out3);
  and and_215 (and_215_out, demultiplexer_15_out1, demultiplexer_3_out0);
  LED led_197 (.in(and_215_out));
  LED led_198 (.in(and_216_out));
  and and_216 (and_216_out, demultiplexer_15_out2, demultiplexer_3_out0);
  and and_217 (and_217_out, demultiplexer_15_out1, demultiplexer_3_out1);
  and and_218 (and_218_out, demultiplexer_15_out2, demultiplexer_3_out1);
  LED led_199 (.in(and_217_out));
  LED led_200 (.in(and_218_out));
  LED led_201 (.in(and_220_out));
  and and_219 (and_219_out, demultiplexer_15_out2, demultiplexer_3_out2);
  and and_220 (and_220_out, demultiplexer_15_out1, demultiplexer_3_out2);
  LED led_202 (.in(and_219_out));
  LED led_203 (.in(and_222_out));
  and and_221 (and_221_out, demultiplexer_15_out2, demultiplexer_3_out3);
  and and_222 (and_222_out, demultiplexer_15_out1, demultiplexer_3_out3);
  LED led_204 (.in(and_221_out));
  and and_223 (and_223_out, demultiplexer_15_out1, demultiplexer_4_out0);
  LED led_205 (.in(and_224_out));
  and and_224 (and_224_out, demultiplexer_15_out2, demultiplexer_4_out0);
  LED led_206 (.in(and_223_out));
  and and_225 (and_225_out, demultiplexer_15_out2, demultiplexer_4_out1);
  LED led_207 (.in(and_225_out));
  LED led_208 (.in(and_226_out));
  and and_226 (and_226_out, demultiplexer_15_out1, demultiplexer_4_out1);
  and and_227 (and_227_out, demultiplexer_15_out1, demultiplexer_4_out2);
  LED led_209 (.in(and_227_out));
  LED led_210 (.in(and_228_out));
  and and_228 (and_228_out, demultiplexer_15_out2, demultiplexer_4_out2);
  and and_229 (and_229_out, demultiplexer_15_out1, demultiplexer_4_out3);
  LED led_211 (.in(and_230_out));
  LED led_212 (.in(and_229_out));
  and and_230 (and_230_out, demultiplexer_15_out2, demultiplexer_4_out3);
  Demultiplexer #(.select(2)) demultiplexer_16 (
    .out0(demultiplexer_16_out0), .out1(demultiplexer_16_out1), .out2(demultiplexer_16_out2),
    .out3(demultiplexer_16_out3), .in(and_198_out), .sel(X_POS_q[1:0]));  // open: en
  LED led_213 (.in(and_231_out));
  and and_231 (and_231_out, demultiplexer_15_out3, demultiplexer_1_out0);
  LED led_214 (.in(and_232_out));
  and and_232 (and_232_out, demultiplexer_15_out3, demultiplexer_1_out1);
  LED led_215 (.in(and_233_out));
  and and_233 (and_233_out, demultiplexer_15_out3, demultiplexer_1_out2);
  LED led_216 (.in(and_234_out));
  and and_234 (and_234_out, demultiplexer_15_out3, demultiplexer_1_out3);
  LED led_217 (.in(and_235_out));
  and and_235 (and_235_out, demultiplexer_15_out3, demultiplexer_2_out0);
  LED led_218 (.in(and_236_out));
  and and_236 (and_236_out, demultiplexer_15_out3, demultiplexer_2_out1);
  LED led_219 (.in(and_237_out));
  and and_237 (and_237_out, demultiplexer_15_out3, demultiplexer_2_out2);
  and and_238 (and_238_out, demultiplexer_15_out3, demultiplexer_2_out3);
  LED led_220 (.in(and_238_out));
  LED led_221 (.in(and_239_out));
  and and_239 (and_239_out, demultiplexer_15_out3, demultiplexer_3_out0);
  and and_240 (and_240_out, demultiplexer_15_out3, demultiplexer_3_out1);
  LED led_222 (.in(and_240_out));
  LED led_223 (.in(and_241_out));
  and and_241 (and_241_out, demultiplexer_15_out3, demultiplexer_3_out2);
  and and_242 (and_242_out, demultiplexer_15_out3, demultiplexer_3_out3);
  LED led_224 (.in(and_242_out));
  and and_243 (and_243_out, demultiplexer_15_out3, demultiplexer_4_out0);
  LED led_225 (.in(and_243_out));
  LED led_226 (.in(and_244_out));
  and and_244 (and_244_out, demultiplexer_15_out3, demultiplexer_4_out1);
  and and_245 (and_245_out, demultiplexer_15_out3, demultiplexer_4_out2);
  LED led_227 (.in(and_245_out));
  and and_246 (and_246_out, demultiplexer_15_out3, demultiplexer_4_out3);
  LED led_228 (.in(and_246_out));
  and and_247 (and_247_out, demultiplexer_16_out0, demultiplexer_1_out0);
  LED led_229 (.in(and_247_out));
  LED led_230 (.in(and_248_out));
  and and_248 (and_248_out, demultiplexer_16_out0, demultiplexer_1_out1);
  and and_249 (and_249_out, demultiplexer_16_out0, demultiplexer_1_out2);
  LED led_231 (.in(and_249_out));
  and and_250 (and_250_out, demultiplexer_16_out0, demultiplexer_1_out3);
  LED led_232 (.in(and_250_out));
  and and_251 (and_251_out, demultiplexer_16_out0, demultiplexer_2_out0);
  LED led_233 (.in(and_251_out));
  LED led_234 (.in(and_252_out));
  and and_252 (and_252_out, demultiplexer_16_out0, demultiplexer_2_out1);
  LED led_235 (.in(and_253_out));
  and and_253 (and_253_out, demultiplexer_16_out0, demultiplexer_2_out2);
  and and_254 (and_254_out, demultiplexer_16_out0, demultiplexer_2_out3);
  LED led_236 (.in(and_254_out));
  and and_255 (and_255_out, demultiplexer_16_out0, demultiplexer_3_out0);
  LED led_237 (.in(and_255_out));
  LED led_238 (.in(and_256_out));
  and and_256 (and_256_out, demultiplexer_16_out0, demultiplexer_3_out1);
  and and_257 (and_257_out, demultiplexer_16_out0, demultiplexer_3_out2);
  LED led_239 (.in(and_257_out));
  and and_258 (and_258_out, demultiplexer_16_out0, demultiplexer_3_out3);
  LED led_240 (.in(and_258_out));
  and and_259 (and_259_out, demultiplexer_16_out0, demultiplexer_4_out0);
  LED led_241 (.in(and_259_out));
  and and_260 (and_260_out, demultiplexer_16_out0, demultiplexer_4_out1);
  LED led_242 (.in(and_260_out));
  LED led_243 (.in(and_261_out));
  and and_261 (and_261_out, demultiplexer_16_out0, demultiplexer_4_out2);
  and and_262 (and_262_out, demultiplexer_16_out0, demultiplexer_4_out3);
  LED led_244 (.in(and_262_out));
  and and_263 (and_263_out, demultiplexer_16_out1, demultiplexer_1_out0);
  LED led_245 (.in(and_263_out));
  and and_264 (and_264_out, demultiplexer_16_out1, demultiplexer_1_out1);
  LED led_246 (.in(and_264_out));
  LED led_247 (.in(and_265_out));
  and and_265 (and_265_out, demultiplexer_16_out1, demultiplexer_1_out2);
  LED led_248 (.in(and_266_out));
  and and_266 (and_266_out, demultiplexer_16_out1, demultiplexer_1_out3);
  LED led_249 (.in(and_267_out));
  and and_267 (and_267_out, demultiplexer_16_out1, demultiplexer_2_out0);
  and and_268 (and_268_out, demultiplexer_16_out1, demultiplexer_2_out1);
  LED led_250 (.in(and_268_out));
  and and_269 (and_269_out, demultiplexer_16_out1, demultiplexer_2_out2);
  LED led_251 (.in(and_269_out));
  LED led_252 (.in(and_270_out));
  and and_270 (and_270_out, demultiplexer_16_out1, demultiplexer_2_out3);
  LED led_253 (.in(and_271_out));
  and and_271 (and_271_out, demultiplexer_16_out1, demultiplexer_3_out0);
  and and_272 (and_272_out, demultiplexer_16_out1, demultiplexer_3_out1);
  LED led_254 (.in(and_272_out));
  and and_273 (and_273_out, demultiplexer_16_out1, demultiplexer_3_out2);
  LED led_255 (.in(and_273_out));
  LED led_256 (.in(and_274_out));
  and and_274 (and_274_out, demultiplexer_16_out1, demultiplexer_3_out3);
  LED led_257 (.in(and_275_out));
  and and_275 (and_275_out, demultiplexer_16_out1, demultiplexer_4_out0);
  and and_276 (and_276_out, demultiplexer_16_out1, demultiplexer_4_out1);
  LED led_258 (.in(and_276_out));
  and and_277 (and_277_out, demultiplexer_16_out1, demultiplexer_4_out2);
  LED led_259 (.in(and_277_out));
  and and_278 (and_278_out, demultiplexer_16_out1, demultiplexer_4_out3);
  LED led_260 (.in(and_278_out));
  LED led_261 (.in(and_279_out));
  and and_279 (and_279_out, demultiplexer_16_out2, demultiplexer_1_out0);
  LED led_262 (.in(and_280_out));
  and and_280 (and_280_out, demultiplexer_16_out2, demultiplexer_1_out1);
  LED led_263 (.in(and_281_out));
  and and_281 (and_281_out, demultiplexer_16_out2, demultiplexer_1_out2);
  LED led_264 (.in(and_282_out));
  and and_282 (and_282_out, demultiplexer_16_out2, demultiplexer_1_out3);
  and and_283 (and_283_out, demultiplexer_16_out2, demultiplexer_2_out0);
  LED led_265 (.in(and_283_out));
  and and_284 (and_284_out, demultiplexer_16_out2, demultiplexer_2_out1);
  LED led_266 (.in(and_284_out));
  and and_285 (and_285_out, demultiplexer_16_out2, demultiplexer_2_out2);
  LED led_267 (.in(and_285_out));
  LED led_268 (.in(and_286_out));
  and and_286 (and_286_out, demultiplexer_16_out2, demultiplexer_2_out3);
  LED led_269 (.in(and_287_out));
  and and_287 (and_287_out, demultiplexer_16_out2, demultiplexer_3_out0);
  LED led_270 (.in(and_288_out));
  and and_288 (and_288_out, demultiplexer_16_out2, demultiplexer_3_out1);
  LED led_271 (.in(and_289_out));
  and and_289 (and_289_out, demultiplexer_16_out2, demultiplexer_3_out2);
  LED led_272 (.in(and_290_out));
  and and_290 (and_290_out, demultiplexer_16_out2, demultiplexer_3_out3);
  and and_291 (and_291_out, demultiplexer_16_out2, demultiplexer_4_out0);
  LED led_273 (.in(and_291_out));
  and and_292 (and_292_out, demultiplexer_16_out2, demultiplexer_4_out1);
  LED led_274 (.in(and_292_out));
  LED led_275 (.in(and_293_out));
  and and_293 (and_293_out, demultiplexer_16_out2, demultiplexer_4_out2);
  LED led_276 (.in(and_294_out));
  and and_294 (and_294_out, demultiplexer_16_out2, demultiplexer_4_out3);
  Clock clock_4 (.out(clock_4_out));
  and and_295 (and_295_out, demultiplexer_16_out3, demultiplexer_1_out0);
  LED led_277 (.in(and_295_out));
  and and_296 (and_296_out, demultiplexer_16_out3, demultiplexer_1_out1);
  LED led_278 (.in(and_296_out));
  LED led_279 (.in(and_297_out));
  and and_297 (and_297_out, demultiplexer_16_out3, demultiplexer_1_out2);
  and and_298 (and_298_out, demultiplexer_16_out3, demultiplexer_1_out3);
  LED led_280 (.in(and_298_out));
  and and_299 (and_299_out, demultiplexer_16_out3, demultiplexer_2_out0);
  LED led_281 (.in(and_299_out));
  and and_300 (and_300_out, demultiplexer_16_out3, demultiplexer_2_out1);
  LED led_282 (.in(and_300_out));
  LED led_283 (.in(and_301_out));
  and and_301 (and_301_out, demultiplexer_16_out3, demultiplexer_2_out2);
  LED led_284 (.in(and_302_out));
  and and_302 (and_302_out, demultiplexer_16_out3, demultiplexer_2_out3);
  and and_303 (and_303_out, demultiplexer_16_out3, demultiplexer_3_out0);
  LED led_285 (.in(and_303_out));
  and and_304 (and_304_out, demultiplexer_16_out3, demultiplexer_3_out1);
  LED led_286 (.in(and_304_out));
  LED led_287 (.in(and_305_out));
  and and_305 (and_305_out, demultiplexer_16_out3, demultiplexer_3_out2);
  LED led_288 (.in(and_306_out));
  and and_306 (and_306_out, demultiplexer_16_out3, demultiplexer_3_out3);
  and and_307 (and_307_out, demultiplexer_16_out3, demultiplexer_4_out0);
  LED led_289 (.in(and_307_out));
  and and_308 (and_308_out, demultiplexer_16_out3, demultiplexer_4_out1);
  LED led_290 (.in(and_308_out));
  LED led_291 (.in(and_309_out));
  and and_309 (and_309_out, demultiplexer_16_out3, demultiplexer_4_out2);
  LED led_292 (.in(and_310_out));
  and and_310 (and_310_out, demultiplexer_16_out3, demultiplexer_4_out3);
  Multiplexer #(.width(4)) multiplexer_3 (
    .in0(adder_5_out), .in1(subtractor_3_out), .out(multiplexer_3_out), .sel(d_ff_1_q));  // open: en
  Multiplexer #(.width(4)) multiplexer_4 (
    .in0(adder_6_out), .in1(subtractor_4_out), .out(multiplexer_4_out), .sel(d_ff_2_q));  // open: en
  Register #(.width(4)) X_POS (.D(multiplexer_3_out), .Q(X_POS_q), .clk(clock_4_out));  // open: en, clr
  Register #(.width(4)) X_VEL (.Q(X_VEL_q), .clk(clock_4_out));  // open: D, en, clr
  D_Flip_Flop d_ff_1 (
    .clk(clock_4_out), .Q(d_ff_1_q), .Qn(d_ff_1_qn), .preset(demultiplexer_16_out3), .reset(and_66_out));  // open: D, en
  Register #(.width(4)) Y_POS (.D(multiplexer_4_out), .Q(Y_POS_q), .clk(clock_4_out));  // open: en, clr
  Register #(.width(4)) Y_VEL (.Q(Y_VEL_q), .clk(clock_4_out));  // open: D, en, clr
  D_Flip_Flop d_ff_2 (
    .clk(clock_4_out), .Q(d_ff_2_q), .Qn(d_ff_2_qn), .preset(demultiplexer_4_out3),
    .reset(demultiplexer_1_out0));  // open: D, en
  Multiplexer #(.width(4)) multiplexer_5 (
    .in0(in_1), .in1(X_POS_q), .out(multiplexer_5_out), .sel(d_ff_1_qn));  // open: en
  Multiplexer #(.width(4)) multiplexer_6 (
    .in0(in_2), .in1(X_VEL_q), .out(multiplexer_6_out), .sel(d_ff_1_qn));  // open: en
  Multiplexer #(.width(4)) multiplexer_7 (
    .in0(in_5), .in1(X_POS_q), .out(multiplexer_7_out), .sel(d_ff_1_q));  // open: en
  Multiplexer #(.width(4)) multiplexer_8 (
    .in0(in_8), .in1(X_VEL_q), .out(multiplexer_8_out), .sel(d_ff_1_q));  // open: en
  Multiplexer #(.width(4)) multiplexer_9 (
    .in0(in_9), .in1(Y_POS_q), .out(multiplexer_9_out), .sel(d_ff_2_qn));  // open: en
  Multiplexer #(.width(4)) multiplexer_10 (
    .in0(in_10), .in1(Y_VEL_q), .out(multiplexer_10_out), .sel(d_ff_2_qn));  // open: en
  Multiplexer #(.width(4)) multiplexer_11 (
    .in0(in_11), .in1(Y_POS_q), .out(multiplexer_11_out), .sel(d_ff_2_q));  // open: en
  Multiplexer #(.width(4)) multiplexer_12 (
    .in0(in_13), .in1(Y_VEL_q), .out(multiplexer_12_out), .sel(d_ff_2_q));  // open: en
  Adder #(.width(4)) adder_5 (.a(multiplexer_5_out), .b(multiplexer_6_out), .out(adder_5_out));  // open: cin, cout
  Subtractor #(.width(4)) subtractor_3 (
    .a(multiplexer_7_out), .b(multiplexer_8_out), .out(subtractor_3_out));  // open: bin, bout
  Adder #(.width(4)) adder_6 (.a(multiplexer_9_out), .b(multiplexer_10_out), .out(adder_6_out));  // open: cin, cout
  Subtractor #(.width(4)) subtractor_4 (
    .a(multiplexer_11_out), .b(multiplexer_12_out), .out(subtractor_4_out));  // open: bin, bout
endmodule
